// Logisim project block33.circ as structural Verilog: 1 circuit, main circuit main
module main (
  input  a,
  input  b,
  input  c,
  input  d,
  input  e,
  input  f,
  output O1,
  output O2,
  output O3
);

  wire and_1_out, and_2_out, and_3_out, and_4_out, and_5_out, and_6_out;

  and and_1 (and_1_out, a, b);
  and and_2 (and_2_out, c, d);
  and and_3 (and_3_out, e, f);
  and and_4 (and_4_out, and_1_out, and_2_out);
  and and_5 (and_5_out, and_2_out, and_3_out);
  and and_6 (and_6_out, and_1_out, and_3_out);
  and and_7 (O1, and_4_out, and_5_out);
  or or_1 (O2, and_5_out, and_6_out);
  xor xor_1 (O3, and_4_out, and_6_out);
endmodule
