// Logisim project block33_pan.circ as structural Verilog: 1 circuit, main circuit main
module main (
  input  a,
  input  b,
  input  c,
  input  d,
  input  e,
  input  f,
  output x,
  output y
);

  wire and_1_out;

  and and_1 (and_1_out, d, e);
  or or_1 (y, e, f);
  and and_2 (x, and_1_out, f);
endmodule
